# Fritzing sketch SmartChess (saved by Fritzing 1.0.2b)

parts:
  J1 = Camdenboss CTB0158-4 [part_number=CTB0158-4 package=THT]
  J2 = Camdenboss CTB0158-4 [part_number=CTB0158-4 package=THT]
  J3 = Camdenboss CTB0158-4 [part_number=CTB0158-4 package=THT]
  Raspberry_PI_4B = Raspberry Pi 4B
  Control_Panel_Backlighting = WS2812 RGB LED strip
  part = Arduino Nano (Rev3.0)
  Screen = Grove OLED 128x96
  Co-ordinate_Backlighting = WS2812 RGB LED strip
  A/1 = Pushbutton [package="[SMD]"]
  B/2 = Pushbutton [package="[SMD]"]
  C/3 = Pushbutton [package="[SMD]"]
  D/4 = Pushbutton [package="[SMD]"]
  E/5 = Pushbutton [package="[SMD]"]
  H/8 = Pushbutton [package="[SMD]"]
  G/7 = Pushbutton [package="[SMD]"]
  F/6 = Pushbutton [package="[SMD]"]
  OK = Pushbutton [package="[SMD]"]
  Hint = Pushbutton [package="[SMD]"]
  Chessboard_squares = WS2812 RGB LED strip
  U1 = Placa TXS0108 [part_number=TXS0108EPW package=TSSOP]

nets:
  GND: J1.terminal_1, J1.terminal_2, J1.terminal_3, J1.terminal_4, Raspberry_PI_4B.GND, Control_Panel_Backlighting.GND#0, part.GND, Screen.GND, A/1.Pin_1, A/1.Pin_2, B/2.Pin_1, B/2.Pin_2, C/3.Pin_1, C/3.Pin_2, D/4.Pin_1, D/4.Pin_2, E/5.Pin_1, H/8.Pin_1, H/8.Pin_2, G/7.Pin_1, G/7.Pin_2, F/6.Pin_1, F/6.Pin_2, OK.Pin_1, Hint.Pin_1, Hint.Pin_2, Chessboard_squares.GND, U1.GND
  5V: J2.pin4, J2.terminal_3, J2.terminal_4, J3.terminal_1, J3.terminal_2, J3.terminal_3, J3.terminal_4, Raspberry_PI_4B.5V, Control_Panel_Backlighting.VCC#1, part.5V, Screen.VCC, Chessboard_squares.VCC, U1.VccB
  N1: Raspberry_PI_4B.3V3, U1.VccA
  N2: Raspberry_PI_4B.GPIO2, Screen.SDA
  N3: Raspberry_PI_4B.GPIO3, Screen.SCL
  N4: Raspberry_PI_4B.GPIO14, U1.A2
  N5: Raspberry_PI_4B.GPIO15, U1.A1
  N6: Control_Panel_Backlighting.DIN, part.D4
  N7: Control_Panel_Backlighting.GND#4, Co-ordinate_Backlighting.GND
  N8: Control_Panel_Backlighting.VCC#5, Co-ordinate_Backlighting.VCC
  N9: Control_Panel_Backlighting.DOUT, Co-ordinate_Backlighting.DIN
  N10: part.D1/TX, U1.B1
  N11: part.D0/RX, U1.B2
  N12: part.D3, Hint.Pin_3, Hint.Pin_4
  N13: part.D5, A/1.Pin_4
  N14: part.D6, B/2.Pin_4
  N15: part.D7, C/3.Pin_4
  N16: part.D8, D/4.Pin_4
  N17: part.D9, E/5.Pin_4
  N18: part.D10, F/6.Pin_4
  N19: part.D11/MOSI, G/7.Pin_4
  N20: part.D12/MISO, H/8.Pin_3, H/8.Pin_4
  N21: part.A5, Chessboard_squares.DIN
  N22: part.A1, OK.Pin_4

notes:
  Raspberry Pi 4 Model B
  A/1
  B/2
  C/3
  D/4
  F/6
  G/7
  E/5
  H/8
  OK
  Hint
  Control Panel Backlighting
  Co-ordinate Backlighting
  Chessboard squares
  TXS0108E
  Arduino Nano

custom parts:
  WS2812 RGB LED strip: WS2812 strip
  Placa TXS0108: This 8-bit non-inverting translator uses two separate configurable power-supply rails. The A port tracks the VCCA pin supply voltage. The VCCA pin accepts any supply voltage between 1.2 V and 3.6 V. The B port tracks the VCCB pin supply voltage. The VCCB pin accepts any supply voltage between 1.65 V and 5.5 V. Two input supply pins allows for low Voltage bidirectional translation between any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
